# Fritzing sketch Untitled Sketch 2 (saved by Fritzing 1.0.4)

parts:
  U1 = LM2596 step down module
  M1 = DOIT Esp32 DevKit v1 (30 pins long, 11 pins width) [part_number=ESP32S-PIN30]
  Keypad4x2 = Keypad Membran 4x4
  M2 = 1 chan 5v relay module
  U2 = RFID RC522 SIP - 8 pins [chip_label="RFID RC522" package="SIP (Single Inline) [THT]"]
  Part1 = LCD1602-I2C
  S1 = MC-38  # not connected
  JACK1 = 2.1mm Barrel Jack with Terminal Block
  L1 = Solenoid

nets:
  N1: U1.IN+, M2.pin_5, JACK1.POS
  GND: U1.IN-, U1.OUT-, M1.GND, M2.pin_2, Part1.GND, JACK1.NEG, L1.pin1
  N2: U1.OUT+, M1.VIN, M2.pin_1
  VCC: M1.3V3, U2.VCC, Part1.VCC
  N3: M1.D4, Keypad4x2.Pin8
  N4: M1.RX2, M2.pin_3
  N5: M1.TX2, U2.RST
  N6: M1.D5, U2.NSS
  N7: M1.D18, U2.SCK
  N8: M1.D19, U2.MISO
  N9: M1.D21, Part1.SDA
  N10: M1.D22, Part1.SCL
  N11: M1.D23, U2.MOSI
  N12: M1.D32, Keypad4x2.Pin7
  N13: M1.D33, Keypad4x2.Pin6
  N14: M1.D25, Keypad4x2.Pin5
  N15: M1.D26, Keypad4x2.Pin4
  N16: M1.D27, Keypad4x2.Pin3
  N17: M1.D14, Keypad4x2.Pin2
  N18: M1.D13, Keypad4x2.Pin1
  N19: M2.pin_4, L1.pin2

notes:
  Khóa từ 12V
  12V DC

custom parts:
  LM2596 step down module: LM2596 DC-DC step down power supply module 3 A.
  DOIT Esp32 DevKit v1 (30 pins long, 11 pins width): The DOIT Esp32 DevKit v1 is one of the development board created by DOIT to evaluate the ESP-WROOM-32 module. It is based on the ESP32 microcontroller that boasts Wifi, Bluetooth, Ethernet and Low Power support all in a single chip. (vanepp) made breadboard work, adjusted pin numbering and labels and reduced size of schematic and cleaned up pcb. This chip is 30pins long (2 x15) and 11 pins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
  Keypad Membran 4x4: Membrane Keypad 4x4 Matrix
  1 chan 5v relay module: 1 Channel 5V Relay Module Board Shield with Optocoupler Support High and Low Level Trigger for Arduino.
  RFID RC522 SIP - 8 pins: A SIP stand-in part for RFID RC522 . With 8 pins on a 300 mil single inline package (SIP) footprint.
  LCD1602-I2C: A standard character display, usually with 2x16 characters. Comes in many colors with LCM1602 IIC attached.
  MC-38: MC-38 Contact Sensor w/ Reed Switch
